# Fritzing sketch climate_meter (saved by Fritzing 0.9.3b)
breadboards: 1

parts:
  Part1 = Arduino Nano (Rev3.0)
  DHT22 = Humidity and Temperature Sensor RHT03
  R1 = Resistor [tolerance=±5% resistance=4.7k package="2512 [SMD]"]
  R2 = Resistor [tolerance=±5% resistance=4.7k package="2512 [SMD]"]
  R3 = Resistor [tolerance=±5% resistance=4.7k package="2512 [SMD]"]
  DS1 = DS18B20 1-Wire Temperature Sensor [part_number=DS18B20]
  DS2 = DS18B20 1-Wire Temperature Sensor [part_number=DS18B20]
  DS3 = DS18B20 1-Wire Temperature Sensor [part_number=DS18B20]
  BMP280 = Barometric Pressure Sensor - BMP180 Breakout (GY-68)

nets:
  GND: Part1.GND, DHT22.GND_2, DS1.GND, DS2.GND, DS3.GND, BMP280.GND
  N1: Part1.D2, DHT22.Data-signal
  N2: Part1.D5, R2.Pin_1, DS1.DQ
  N3: Part1.D6, R1.Pin_1, DS2.DQ
  N4: Part1.D7, R3.Pin_1, DS3.DQ
  VDD: Part1.5V, DHT22.Vcc, R1.Pin_0, R2.Pin_0, R3.Pin_0, DS1.VDD, DS2.VDD, DS3.VDD
  N5: Part1.A5, BMP280.SCL
  N6: Part1.A4, BMP280.SDA
  3V3: Part1.3V3, BMP280.VCC
